// Logisim project Project P3.circ as structural Verilog: 4 circuits, main circuit regfile
module CPU_old (
  input  [31:0] DataFromBus,
  output [15:0] AddressToBus,
  output BusWriteEnable,
  output [31:0] DataToBus
);

  wire alu_1_equal, and_1_out, and_2_out, clock_1_out, control_1_aluvmemselect, control_1_beq, control_1_bne,
       control_1_imm_sel, control_1_j, control_1_jal, control_1_jalr, control_1_jr, control_1_we_regfile,
       or_1_out, or_2_out, or_3_out, or_4_out;
  wire [3:0] control_1_alu_operation;
  wire [4:0] control_1_rd_select, control_1_rs_select, control_1_rt_select;
  wire [15:0] bit_extender_3_out, control_1_imm, shifter_1_out;
  wire [25:0] bit_extender_4_out, shifter_2_out;
  wire [31:0] adder_1_out, adder_2_out, alu_1_res, bit_extender_1_out, bit_extender_2_out,
       bit_extender_5_out, multiplexer_1_out, multiplexer_2_out, multiplexer_3_out, multiplexer_4_out,
       multiplexer_5_out, multiplexer_6_out, ProgramCounter_q, regfile_1_rs_data, rom_1_data, shifter_3_out,
       shifter_4_out;

  Shifter #(.width(16)) shifter_1 (.in(control_1_imm), .\dist (4'b0010), .out(shifter_1_out));
  Adder #(.width(32)) adder_1 (.a(ProgramCounter_q), .b(32'h4), .out(adder_1_out));  // open: cin, cout
  assign bit_extender_1_out = {{16{shifter_1_out[15]}}, shifter_1_out};  // Bit_Extender bit_extender_1
  Adder #(.width(32)) adder_2 (.a(adder_1_out), .b(bit_extender_1_out), .out(adder_2_out));  // open: cin, cout
  Shifter #(.width(26)) shifter_2 (.in(bit_extender_4_out), .\dist (5'b00010), .out(shifter_2_out));
  and and_1 (and_1_out, control_1_bne, ~alu_1_equal);  // AND_Gate
  and and_2 (and_2_out, control_1_beq, alu_1_equal);
  or or_1 (or_1_out, and_1_out, and_2_out);
  Multiplexer #(.width(32)) multiplexer_1 (
    .in0(adder_1_out), .in1(adder_2_out), .out(multiplexer_1_out), .sel(or_1_out));
  assign bit_extender_2_out = {{6{shifter_2_out[25]}}, shifter_2_out};  // Bit_Extender bit_extender_2
  or or_2 (or_2_out, control_1_jalr, control_1_jr);
  or or_3 (or_3_out, control_1_jal, control_1_jalr, control_1_jr, control_1_j);
  Multiplexer #(.width(32)) multiplexer_2 (
    .in0(multiplexer_1_out), .in1(multiplexer_3_out), .out(multiplexer_2_out), .sel(or_3_out));
  Multiplexer #(.width(32)) multiplexer_3 (
    .in0(bit_extender_2_out), .in1(regfile_1_rs_data), .out(multiplexer_3_out), .sel(or_2_out));
  Register #(.width(32)) ProgramCounter (
    .D(multiplexer_2_out), .en(1'b1), .clk(clock_1_out), .Q(ProgramCounter_q));  // open: clr
  Clock clock_1 (.out(clock_1_out));
  Shifter #(.shift("lr"), .width(32)) shifter_3 (.in(ProgramCounter_q), .\dist (5'b00010), .out(shifter_3_out));
  ROM #(.addrWidth(16), .dataWidth(32)) rom_1 (.addr(bit_extender_3_out), .data(rom_1_data));
  Bit_Extender #(.in_width(32)) bit_extender_3 (.in(shifter_3_out), .out(bit_extender_3_out));
  Bit_Extender #(.in_width(32), .out_width(26)) bit_extender_4 (.in(rom_1_data), .out(bit_extender_4_out));
  // Probe on rom_1_data
  Multiplexer #(.width(32)) multiplexer_4 (
    .in0(alu_1_res), .in1(DataFromBus), .out(multiplexer_4_out), .sel(control_1_aluvmemselect));
  or or_4 (or_4_out, control_1_jal, control_1_jalr);
  Multiplexer #(.width(32)) multiplexer_5 (
    .in0(multiplexer_4_out), .in1(adder_1_out), .out(multiplexer_5_out), .sel(or_4_out));
  regfile regfile_1 (
    .write_e(control_1_we_regfile), .rd(control_1_rd_select), .rt(control_1_rt_select),
    .rs(control_1_rs_select), .rd_data(multiplexer_5_out), .rs_data(regfile_1_rs_data), .rt_data(DataToBus));
  Control control_1 (
    .Instruction(rom_1_data), .we_regfile(control_1_we_regfile), .we_mem(BusWriteEnable),
    .imm_sel(control_1_imm_sel), .jr(control_1_jr), .jalr(control_1_jalr),
    .ALUvMEMselect(control_1_aluvmemselect), .j(control_1_j), .jal(control_1_jal), .beq(control_1_beq),
    .bne(control_1_bne), .rd_select(control_1_rd_select), .rt_select(control_1_rt_select),
    .rs_select(control_1_rs_select), .imm(control_1_imm), .ALU_operation(control_1_alu_operation));
  assign bit_extender_5_out = {{16{control_1_imm[15]}}, control_1_imm};  // Bit_Extender bit_extender_5
  Multiplexer #(.width(32)) multiplexer_6 (
    .in0(DataToBus), .in1(bit_extender_5_out), .out(multiplexer_6_out), .sel(control_1_imm_sel));
  ALU alu_1 (
    .Control(control_1_alu_operation), .OP1(regfile_1_rs_data), .OP2(multiplexer_6_out), .temp_OP(DataToBus),
    .equal(alu_1_equal), .Res(alu_1_res));
  Shifter #(.shift("lr"), .width(32)) shifter_4 (.in(alu_1_res), .\dist (5'b00010), .out(shifter_4_out));
  Bit_Extender #(.in_width(32)) bit_extender_6 (.in(shifter_4_out), .out(AddressToBus));

  // Notes on the sheet:
  //   offset: (word addressed)
  //   PC + 4
  //   label: for j, jal (word addressed)
  //   if branch is to be taken
  //   PC + 4 + Offset
  //   jr/jalr
  //   register: for jr, jalr (byte addressed)
  //   any j*
  //   1 if two registers are ==
  //   contents of rom_1 (hex, n*v repeats v):
  //   20080000 20090004 200a0008 8d0b0000 8d2c0000 200f000c 8dee0000 1c0f809 ad4d0000 8000009 16c6820
  //   3e00008
  //   immediate
  //   label to jump to
  //   rs-data
  //   probe to help test the value in a wire
  //   ALU
  //   MEM
  //   PC + 4
  //   jal/jalr
  //   value from memory
  //   value from ALU
endmodule

module regfile (
  input  [31:0] rd_data,
  input  [4:0] rd,
  input  write_e,
  input  [4:0] rt,
  input  [4:0] rs,
  output [31:0] rs_data,
  output [31:0] rt_data
);

  wire clock_1_out, clock_2_out, clock_3_out, clock_4_out, clock_5_out, clock_6_out, clock_7_out,
       clock_8_out, clock_9_out, clock_10_out, clock_11_out, clock_12_out, clock_13_out, clock_14_out,
       clock_15_out, clock_16_out, clock_17_out, clock_18_out, clock_19_out, clock_20_out, clock_21_out,
       clock_22_out, clock_23_out, clock_24_out, clock_25_out, clock_26_out, clock_27_out, clock_28_out,
       clock_29_out, clock_30_out, clock_31_out, clock_32_out, demultiplexer_1_out1, demultiplexer_1_out2,
       demultiplexer_1_out3, demultiplexer_1_out4, demultiplexer_1_out5, demultiplexer_1_out6,
       demultiplexer_1_out7, demultiplexer_1_out8, demultiplexer_1_out9, demultiplexer_1_out10,
       demultiplexer_1_out11, demultiplexer_1_out12, demultiplexer_1_out13, demultiplexer_1_out14,
       demultiplexer_1_out15, demultiplexer_1_out16, demultiplexer_1_out17, demultiplexer_1_out18,
       demultiplexer_1_out19, demultiplexer_1_out20, demultiplexer_1_out21, demultiplexer_1_out22,
       demultiplexer_1_out23, demultiplexer_1_out24, demultiplexer_1_out25, demultiplexer_1_out26,
       demultiplexer_1_out27, demultiplexer_1_out28, demultiplexer_1_out29, demultiplexer_1_out30,
       demultiplexer_1_out31;
  wire [31:0] R0_r0_q, R1_at_q, R2_v0_q, R3_v1_q, R4_a0_q, R5_a1_q, R6_a2_q, R7_a3_q, R8_t0_q, R9_t1_q,
       R10_t2_q, R11_t3_q, R12_t4_q, R13_t5_q, R14_t6_q, R15_t7_q, R16_s0_q, R17_s1_q, R18_s2_q, R19_s3_q,
       R20_s4_q, R21_s5_q, R22_s6_q, R23_s7_q, R24_t8_q, R25_t9_q, R26_k0_q, R27_k1_q, R28_gp_q, R29_sp_q,
       R30_s8_q, R31_ra_q;

  Demultiplexer #(.select(5)) demultiplexer_1 (
    .out1(demultiplexer_1_out1), .out2(demultiplexer_1_out2), .out3(demultiplexer_1_out3),
    .out4(demultiplexer_1_out4), .out5(demultiplexer_1_out5), .out6(demultiplexer_1_out6),
    .out7(demultiplexer_1_out7), .out8(demultiplexer_1_out8), .out9(demultiplexer_1_out9),
    .out10(demultiplexer_1_out10), .out11(demultiplexer_1_out11), .out12(demultiplexer_1_out12),
    .out13(demultiplexer_1_out13), .out14(demultiplexer_1_out14), .out15(demultiplexer_1_out15),
    .out16(demultiplexer_1_out16), .out17(demultiplexer_1_out17), .out18(demultiplexer_1_out18),
    .out19(demultiplexer_1_out19), .out20(demultiplexer_1_out20), .out21(demultiplexer_1_out21),
    .out22(demultiplexer_1_out22), .out23(demultiplexer_1_out23), .out24(demultiplexer_1_out24),
    .out25(demultiplexer_1_out25), .out26(demultiplexer_1_out26), .out27(demultiplexer_1_out27),
    .out28(demultiplexer_1_out28), .out29(demultiplexer_1_out29), .out30(demultiplexer_1_out30),
    .out31(demultiplexer_1_out31), .in(write_e), .sel(rd));  // open: out0
  Register #(.width(32)) R0_r0 (.D({32{1'b0}}), .en(1'b1), .clk(clock_1_out), .Q(R0_r0_q));  // open: clr
  Clock clock_1 (.out(clock_1_out));
  Register #(.width(32)) R1_at (.D(rd_data), .en(demultiplexer_1_out1), .clk(clock_2_out), .Q(R1_at_q));  // open: clr
  Clock clock_2 (.out(clock_2_out));
  Register #(.width(32)) R2_v0 (.D(rd_data), .en(demultiplexer_1_out2), .clk(clock_3_out), .Q(R2_v0_q));  // open: clr
  Clock clock_3 (.out(clock_3_out));
  Register #(.width(32)) R3_v1 (.D(rd_data), .en(demultiplexer_1_out3), .clk(clock_4_out), .Q(R3_v1_q));  // open: clr
  Clock clock_4 (.out(clock_4_out));
  Register #(.width(32)) R4_a0 (.D(rd_data), .en(demultiplexer_1_out4), .clk(clock_5_out), .Q(R4_a0_q));  // open: clr
  Clock clock_5 (.out(clock_5_out));
  Register #(.width(32)) R5_a1 (.D(rd_data), .en(demultiplexer_1_out5), .clk(clock_6_out), .Q(R5_a1_q));  // open: clr
  Clock clock_6 (.out(clock_6_out));
  Register #(.width(32)) R6_a2 (.D(rd_data), .en(demultiplexer_1_out6), .clk(clock_7_out), .Q(R6_a2_q));  // open: clr
  Clock clock_7 (.out(clock_7_out));
  Register #(.width(32)) R7_a3 (.D(rd_data), .en(demultiplexer_1_out7), .clk(clock_8_out), .Q(R7_a3_q));  // open: clr
  Clock clock_8 (.out(clock_8_out));
  Register #(.width(32)) R8_t0 (.D(rd_data), .en(demultiplexer_1_out8), .clk(clock_9_out), .Q(R8_t0_q));  // open: clr
  Clock clock_9 (.out(clock_9_out));
  Register #(.width(32)) R9_t1 (.D(rd_data), .en(demultiplexer_1_out9), .clk(clock_10_out), .Q(R9_t1_q));  // open: clr
  Clock clock_10 (.out(clock_10_out));
  Register #(.width(32)) R10_t2 (
    .D(rd_data), .en(demultiplexer_1_out10), .clk(clock_11_out), .Q(R10_t2_q));  // open: clr
  Clock clock_11 (.out(clock_11_out));
  Register #(.width(32)) R11_t3 (
    .D(rd_data), .en(demultiplexer_1_out11), .clk(clock_12_out), .Q(R11_t3_q));  // open: clr
  Clock clock_12 (.out(clock_12_out));
  Register #(.width(32)) R12_t4 (
    .D(rd_data), .en(demultiplexer_1_out12), .clk(clock_13_out), .Q(R12_t4_q));  // open: clr
  Clock clock_13 (.out(clock_13_out));
  Register #(.width(32)) R13_t5 (
    .D(rd_data), .en(demultiplexer_1_out13), .clk(clock_14_out), .Q(R13_t5_q));  // open: clr
  Clock clock_14 (.out(clock_14_out));
  Register #(.width(32)) R14_t6 (
    .D(rd_data), .en(demultiplexer_1_out14), .clk(clock_15_out), .Q(R14_t6_q));  // open: clr
  Clock clock_15 (.out(clock_15_out));
  Register #(.width(32)) R15_t7 (
    .D(rd_data), .en(demultiplexer_1_out15), .clk(clock_16_out), .Q(R15_t7_q));  // open: clr
  Clock clock_16 (.out(clock_16_out));
  Register #(.width(32)) R16_s0 (
    .D(rd_data), .en(demultiplexer_1_out16), .clk(clock_17_out), .Q(R16_s0_q));  // open: clr
  Clock clock_17 (.out(clock_17_out));
  Register #(.width(32)) R17_s1 (
    .D(rd_data), .en(demultiplexer_1_out17), .clk(clock_18_out), .Q(R17_s1_q));  // open: clr
  Clock clock_18 (.out(clock_18_out));
  Register #(.width(32)) R18_s2 (
    .D(rd_data), .en(demultiplexer_1_out18), .clk(clock_19_out), .Q(R18_s2_q));  // open: clr
  Clock clock_19 (.out(clock_19_out));
  Register #(.width(32)) R19_s3 (
    .D(rd_data), .en(demultiplexer_1_out19), .clk(clock_20_out), .Q(R19_s3_q));  // open: clr
  Clock clock_20 (.out(clock_20_out));
  Register #(.width(32)) R20_s4 (
    .D(rd_data), .en(demultiplexer_1_out20), .clk(clock_21_out), .Q(R20_s4_q));  // open: clr
  Clock clock_21 (.out(clock_21_out));
  Register #(.width(32)) R21_s5 (
    .D(rd_data), .en(demultiplexer_1_out21), .clk(clock_22_out), .Q(R21_s5_q));  // open: clr
  Clock clock_22 (.out(clock_22_out));
  Register #(.width(32)) R22_s6 (
    .D(rd_data), .en(demultiplexer_1_out22), .clk(clock_23_out), .Q(R22_s6_q));  // open: clr
  Clock clock_23 (.out(clock_23_out));
  Register #(.width(32)) R23_s7 (
    .D(rd_data), .en(demultiplexer_1_out23), .clk(clock_24_out), .Q(R23_s7_q));  // open: clr
  Clock clock_24 (.out(clock_24_out));
  Register #(.width(32)) R24_t8 (
    .D(rd_data), .en(demultiplexer_1_out24), .clk(clock_25_out), .Q(R24_t8_q));  // open: clr
  Clock clock_25 (.out(clock_25_out));
  Register #(.width(32)) R25_t9 (
    .D(rd_data), .en(demultiplexer_1_out25), .clk(clock_26_out), .Q(R25_t9_q));  // open: clr
  Clock clock_26 (.out(clock_26_out));
  Register #(.width(32)) R26_k0 (
    .D(rd_data), .en(demultiplexer_1_out26), .clk(clock_27_out), .Q(R26_k0_q));  // open: clr
  Clock clock_27 (.out(clock_27_out));
  Register #(.width(32)) R27_k1 (
    .D(rd_data), .en(demultiplexer_1_out27), .clk(clock_28_out), .Q(R27_k1_q));  // open: clr
  Clock clock_28 (.out(clock_28_out));
  Register #(.width(32)) R28_gp (
    .D(rd_data), .en(demultiplexer_1_out28), .clk(clock_29_out), .Q(R28_gp_q));  // open: clr
  Clock clock_29 (.out(clock_29_out));
  Register #(.width(32)) R29_sp (
    .D(rd_data), .en(demultiplexer_1_out29), .clk(clock_30_out), .Q(R29_sp_q));  // open: clr
  Clock clock_30 (.out(clock_30_out));
  Register #(.width(32)) R30_s8 (
    .D(rd_data), .en(demultiplexer_1_out30), .clk(clock_31_out), .Q(R30_s8_q));  // open: clr
  Clock clock_31 (.out(clock_31_out));
  Register #(.width(32)) R31_ra (
    .D(rd_data), .en(demultiplexer_1_out31), .clk(clock_32_out), .Q(R31_ra_q));  // open: clr
  Clock clock_32 (.out(clock_32_out));
  Multiplexer #(.select(5), .width(32)) multiplexer_1 (
    .in0(R0_r0_q), .in1(R1_at_q), .in2(R2_v0_q), .in3(R3_v1_q), .in4(R4_a0_q), .in5(R5_a1_q), .in6(R6_a2_q),
    .in7(R7_a3_q), .in8(R8_t0_q), .in9(R9_t1_q), .in10(R10_t2_q), .in11(R11_t3_q), .in12(R12_t4_q),
    .in13(R13_t5_q), .in14(R14_t6_q), .in15(R15_t7_q), .in16(R16_s0_q), .in17(R17_s1_q), .in18(R18_s2_q),
    .in19(R19_s3_q), .in20(R20_s4_q), .in21(R21_s5_q), .in22(R22_s6_q), .in23(R23_s7_q), .in24(R24_t8_q),
    .in25(R25_t9_q), .in26(R26_k0_q), .in27(R27_k1_q), .in28(R28_gp_q), .in29(R29_sp_q), .in30(R30_s8_q),
    .in31(R31_ra_q), .out(rs_data), .sel(rs));
  Multiplexer #(.select(5), .width(32)) multiplexer_2 (
    .in0(R0_r0_q), .in1(R1_at_q), .in2(R2_v0_q), .in3(R3_v1_q), .in4(R4_a0_q), .in5(R5_a1_q), .in6(R6_a2_q),
    .in7(R7_a3_q), .in8(R8_t0_q), .in9(R9_t1_q), .in10(R10_t2_q), .in11(R11_t3_q), .in12(R12_t4_q),
    .in13(R13_t5_q), .in14(R14_t6_q), .in15(R15_t7_q), .in16(R16_s0_q), .in17(R17_s1_q), .in18(R18_s2_q),
    .in19(R19_s3_q), .in20(R20_s4_q), .in21(R21_s5_q), .in22(R22_s6_q), .in23(R23_s7_q), .in24(R24_t8_q),
    .in25(R25_t9_q), .in26(R26_k0_q), .in27(R27_k1_q), .in28(R28_gp_q), .in29(R29_sp_q), .in30(R30_s8_q),
    .in31(R31_ra_q), .out(rt_data), .sel(rt));
endmodule

module ALU (
  input  [3:0] Control,
  input  [31:0] OP1,
  input  [31:0] OP2,
  input  [31:0] temp_OP,
  output [31:0] Res,
  output equal
);

  wire clock_1_out, clock_2_out, comparator_1_lt, comparator_3_eq, comparator_4_eq, or_1_out;
  wire [4:0] bit_extender_3_out, bit_extender_4_out;
  wire [31:0] adder_1_out, bit_extender_5_out, divider_1_out, divider_1_rem, HI_q, LO_q, shifter_1_out,
       shifter_2_out, subtractor_1_out, subtractor_2_out;
  wire [63:0] bit_extender_1_out, bit_extender_2_out, multiplexer_2_out, multiplier_1_out;

  Adder #(.width(32)) adder_1 (.a(OP1), .b(OP2), .out(adder_1_out));  // open: cin, cout
  Subtractor #(.width(32)) subtractor_1 (.a(OP1), .b(OP2), .out(subtractor_1_out));  // open: bin, bout
  assign bit_extender_1_out = {{32{OP1[31]}}, OP1};  // Bit_Extender bit_extender_1
  assign bit_extender_2_out = {{32{OP2[31]}}, OP2};  // Bit_Extender bit_extender_2
  Divider #(.mode("twosComplement"), .width(32)) divider_1 (
    .a(OP1), .b(OP2), .out(divider_1_out), .rem(divider_1_rem));  // open: upper
  Comparator #(.width(32)) comparator_1 (.a(OP1), .b(OP2), .lt(comparator_1_lt));  // open: gt, eq
  Shifter #(.width(32)) shifter_1 (.in(OP1), .\dist (bit_extender_3_out), .out(shifter_1_out));
  Bit_Extender #(.in_width(32), .out_width(5)) bit_extender_3 (.in(OP2), .out(bit_extender_3_out));
  Shifter #(.shift("lr"), .width(32)) shifter_2 (.in(OP1), .\dist (bit_extender_4_out), .out(shifter_2_out));
  Bit_Extender #(.in_width(32), .out_width(5)) bit_extender_4 (.in(OP2), .out(bit_extender_4_out));
  Comparator #(.width(32)) comparator_2 (.a(OP1), .b(temp_OP), .eq(equal));  // open: gt, lt
  assign bit_extender_5_out = {{31{comparator_1_lt}}, comparator_1_lt};  // Bit_Extender bit_extender_5
  Multiplier #(.width(64)) multiplier_1 (
    .a(bit_extender_1_out), .b(bit_extender_2_out), .out(multiplier_1_out));  // open: cin, cout
  Subtractor #(.width(32)) subtractor_2 (
    .a({32{1'b0}}), .b(bit_extender_5_out), .out(subtractor_2_out));  // open: bin, bout
  Multiplexer #(.select(4), .width(32)) multiplexer_1 (
    .in0(adder_1_out), .in1(subtractor_1_out), .in6(shifter_1_out), .in7(shifter_2_out),
    .in8(subtractor_2_out), .in9(OP2), .in10(OP2), .out(Res), .sel(Control));  // open: in2, in3, in4, in5, in11, in12, in13, in14, in15
  Multiplexer #(.select(4), .width(64)) multiplexer_2 (
    .in2(multiplier_1_out), .out(multiplexer_2_out), .sel(Control));  // open: in0, in1, in3, in4, in5, in6, in7, in8, in9, in10, in11, in12, in13, in14, in15
  Multiplexer #(.select(4), .width(32)) multiplexer_3 (
    .in3(divider_1_out), .out(multiplexer_2_out[31:0]), .sel(Control));  // open: in0, in1, in2, in4, in5, in6, in7, in8, in9, in10, in11, in12, in13, in14, in15
  Multiplexer #(.select(4), .width(32)) multiplexer_4 (
    .in3(divider_1_rem), .out(multiplexer_2_out[63:32]), .sel(Control));  // open: in0, in1, in2, in4, in5, in6, in7, in8, in9, in10, in11, in12, in13, in14, in15
  Comparator #(.width(4)) comparator_3 (.a(Control), .b(4'b0011), .eq(comparator_3_eq));  // open: gt, lt
  Comparator #(.width(4)) comparator_4 (.a(Control), .b(4'b0010), .eq(comparator_4_eq));  // open: gt, lt
  or or_1 (or_1_out, comparator_3_eq, comparator_4_eq);
  Register #(.width(32)) LO (.D(multiplexer_2_out[31:0]), .en(or_1_out), .clk(clock_1_out), .Q(LO_q));  // open: clr
  Clock clock_1 (.out(clock_1_out));
  Register #(.width(32)) HI (.D(multiplexer_2_out[63:32]), .en(or_1_out), .clk(clock_2_out), .Q(HI_q));  // open: clr
  Clock clock_2 (.out(clock_2_out));
  Multiplexer #(.select(4), .width(32)) multiplexer_5 (
    .in4(LO_q), .in5(HI_q), .out(Res), .sel(Control));  // open: in0, in1, in2, in3, in6, in7, in8, in9, in10, in11, in12, in13, in14, in15
endmodule

module Control (
  input  [31:0] Instruction,
  output [3:0] ALU_operation,
  output we_regfile,
  output we_mem,
  output imm_sel,
  output jr,
  output jalr,
  output [15:0] imm,
  output [4:0] rd_select,
  output [4:0] rt_select,
  output [4:0] rs_select,
  output ALUvMEMselect,
  output j,
  output jal,
  output beq,
  output bne
);

  wire and_1_out, and_2_out, and_3_out, and_4_out, and_5_out, and_6_out, and_7_out, and_8_out, and_9_out,
       and_11_out, and_12_out, comparator_1_eq, comparator_2_eq, comparator_3_eq, comparator_4_eq,
       comparator_5_eq, comparator_6_eq, comparator_7_eq, comparator_8_eq, comparator_9_eq, comparator_10_eq,
       comparator_11_eq, comparator_12_eq, comparator_13_eq, comparator_14_eq, comparator_20_eq, or_2_out,
       or_3_out, or_4_out, or_5_out, or_6_out, or_7_out, or_8_out, or_9_out, or_12_out, undriven;
  wire [4:0] multiplexer_15_out, multiplexer_17_out, multiplexer_19_out;
  wire [15:0] bit_extender_1_out;

  // Probe on comparator_13_eq
  Comparator #(.width(6)) comparator_1 (.a(6'b100000), .b(Instruction[5:0]), .eq(comparator_1_eq));  // open: gt, lt
  Comparator #(.width(6)) comparator_2 (.a(6'b100010), .b(Instruction[5:0]), .eq(comparator_2_eq));  // open: gt, lt
  Comparator #(.width(6)) comparator_3 (.a(6'b011000), .b(Instruction[5:0]), .eq(comparator_3_eq));  // open: gt, lt
  Comparator #(.width(6)) comparator_4 (.a(6'b011010), .b(Instruction[5:0]), .eq(comparator_4_eq));  // open: gt, lt
  Comparator #(.width(6)) comparator_5 (.a(6'b010010), .b(Instruction[5:0]), .eq(comparator_5_eq));  // open: gt, lt
  Comparator #(.width(6)) comparator_6 (.a(6'b010000), .b(Instruction[5:0]), .eq(comparator_6_eq));  // open: gt, lt
  Comparator #(.width(6)) comparator_7 (.a({6{1'b0}}), .b(Instruction[5:0]), .eq(comparator_7_eq));  // open: gt, lt
  Comparator #(.width(6)) comparator_8 (.a(6'b000010), .b(Instruction[5:0]), .eq(comparator_8_eq));  // open: gt, lt
  Comparator #(.width(6)) comparator_9 (.a(6'b101010), .b(Instruction[5:0]), .eq(comparator_9_eq));  // open: gt, lt
  Comparator #(.width(6)) comparator_10 (.a(6'b001000), .b(Instruction[31:26]), .eq(comparator_10_eq));  // open: gt, lt
  Comparator #(.width(6)) comparator_11 (.a(6'b001000), .b(Instruction[5:0]), .eq(comparator_11_eq));  // open: gt, lt
  Comparator #(.width(6)) comparator_12 (.a(6'b001001), .b(Instruction[5:0]), .eq(comparator_12_eq));  // open: gt, lt
  Comparator #(.width(6)) comparator_13 (.a({6{1'b0}}), .b(Instruction[31:26]), .eq(comparator_13_eq));  // open: gt, lt
  Comparator #(.width(6)) comparator_14 (.a(6'b100011), .b(Instruction[31:26]), .eq(comparator_14_eq));  // open: gt, lt
  Comparator #(.width(6)) comparator_15 (.a(6'b101011), .b(Instruction[31:26]), .eq(we_mem));  // open: gt, lt
  Comparator #(.width(6)) comparator_16 (.a(6'b000010), .b(Instruction[31:26]), .eq(j));  // open: gt, lt
  Comparator #(.width(6)) comparator_17 (.a(6'b000011), .b(Instruction[31:26]), .eq(jal));  // open: gt, lt
  Comparator #(.width(6)) comparator_18 (.a(6'b000100), .b(Instruction[31:26]), .eq(beq));  // open: gt, lt
  Comparator #(.width(6)) comparator_19 (.a(6'b000101), .b(Instruction[31:26]), .eq(bne));  // open: gt, lt
  and and_1 (and_1_out, comparator_1_eq, comparator_13_eq);
  and and_2 (and_2_out, comparator_2_eq, comparator_13_eq);
  and and_3 (and_3_out, comparator_3_eq, comparator_13_eq);
  and and_4 (and_4_out, comparator_4_eq, comparator_13_eq);
  and and_5 (and_5_out, comparator_5_eq, comparator_13_eq);
  and and_6 (and_6_out, comparator_6_eq, comparator_13_eq);
  and and_7 (and_7_out, comparator_7_eq, comparator_13_eq);
  and and_8 (and_8_out, comparator_8_eq, comparator_13_eq);
  and and_9 (and_9_out, comparator_9_eq, comparator_13_eq);
  and and_10 (jr, comparator_11_eq, comparator_13_eq);
  and and_11 (and_11_out, comparator_12_eq, comparator_13_eq);
  Comparator #(.width(6)) comparator_20 (.a(Instruction[5:0]), .b(6'b001100), .eq(comparator_20_eq));  // open: gt, lt
  assign bit_extender_1_out = {{11{Instruction[10]}}, Instruction[10:6]};  // Bit_Extender bit_extender_1
  Multiplexer #(.width(4)) multiplexer_1 (.in1(4'b0000), .out(ALU_operation), .sel(and_1_out));  // open: in0
  Multiplexer #(.width(4)) multiplexer_2 (.in1(4'b0001), .out(ALU_operation), .sel(and_2_out));  // open: in0
  Multiplexer #(.width(4)) multiplexer_3 (.in1(4'b0010), .out(ALU_operation), .sel(and_3_out));  // open: in0
  Multiplexer #(.width(4)) multiplexer_4 (.in1(4'b0011), .out(ALU_operation), .sel(and_4_out));  // open: in0
  Multiplexer #(.width(4)) multiplexer_5 (.in1(4'b0100), .out(ALU_operation), .sel(and_5_out));  // open: in0
  Multiplexer #(.width(4)) multiplexer_6 (.in1(4'b0101), .out(ALU_operation), .sel(and_6_out));  // open: in0
  Multiplexer #(.width(4)) multiplexer_7 (.in1(4'b0110), .out(ALU_operation), .sel(and_7_out));  // open: in0
  Multiplexer #(.width(4)) multiplexer_8 (.in1(4'b0111), .out(ALU_operation), .sel(and_8_out));  // open: in0
  Multiplexer #(.width(4)) multiplexer_9 (.in1(4'b1000), .out(ALU_operation), .sel(and_9_out));  // open: in0
  Multiplexer #(.width(4)) multiplexer_10 (.in1(4'b0000), .out(ALU_operation), .sel(comparator_10_eq));  // open: in0
  and and_12 (and_12_out, comparator_20_eq, comparator_13_eq);
  Multiplexer #(.width(4)) multiplexer_11 (.in1(4'b0000), .out(ALU_operation), .sel(comparator_14_eq));  // open: in0
  Multiplexer #(.width(4)) multiplexer_12 (.in1(4'b0000), .out(ALU_operation), .sel(we_mem));  // open: in0
  Multiplexer #(.width(4)) multiplexer_13 (.in1(4'b1001), .out(ALU_operation), .sel(beq));  // open: in0
  Multiplexer #(.width(4)) multiplexer_14 (.in1(4'b1010), .out(ALU_operation), .sel(bne));  // open: in0
  // Probe on and_11_out
  or or_1 (jalr, and_11_out, and_12_out);
  // Probe on undriven
  or or_2 (or_2_out, jal, or_8_out, or_7_out, or_5_out, jalr, jalr);
  Multiplexer #(.width(5)) multiplexer_15 (
    .in1(Instruction[15:11]), .out(multiplexer_15_out), .sel(or_2_out));  // open: in0
  or or_3 (or_3_out, bne, beq, comparator_14_eq, comparator_10_eq, or_5_out, or_8_out, or_6_out, we_mem);
  Multiplexer #(.width(5)) multiplexer_16 (.in1(Instruction[20:16]), .out(rt_select), .sel(or_3_out));  // open: in0
  or or_4 (or_4_out, jalr, jalr, jr, or_6_out, comparator_10_eq, or_5_out, comparator_14_eq, we_mem, beq, bne);
  Multiplexer #(.width(5)) multiplexer_17 (
    .in1(Instruction[25:21]), .out(multiplexer_17_out), .sel(or_4_out));  // open: in0
  or or_5 (or_5_out, and_1_out, and_2_out, and_9_out);
  or or_6 (or_6_out, and_3_out, and_4_out);
  or or_7 (or_7_out, and_5_out, and_6_out);
  or or_8 (or_8_out, and_7_out, and_8_out);
  or or_9 (or_9_out, we_mem, comparator_10_eq, comparator_14_eq, beq, bne);
  Multiplexer #(.width(16)) multiplexer_18 (
    .in0(bit_extender_1_out), .in1(Instruction[15:0]), .out(imm), .sel(or_9_out));
  or or_10 (we_regfile, comparator_14_eq, or_7_out, or_5_out, jal, or_8_out, comparator_10_eq, jalr, jalr);
  or or_11 (imm_sel, or_8_out, or_9_out);
  or or_12 (or_12_out, comparator_10_eq, comparator_14_eq);
  or or_13 (ALUvMEMselect, jr, jal, comparator_14_eq, we_mem, jalr);
  // Probe on jalr
  Multiplexer #(.width(5)) multiplexer_19 (
    .in0(multiplexer_15_out), .in1({5{1'b1}}), .out(multiplexer_19_out), .sel(jal));
  Multiplexer #(.width(5)) multiplexer_20 (.in0(multiplexer_19_out), .in1(rt_select), .out(rd_select), .sel(or_12_out));
  Multiplexer #(.width(5)) multiplexer_21 (.in0(multiplexer_17_out), .in1(rt_select), .out(rs_select), .sel(or_8_out));

  // Notes on the sheet:
  //   add
  //   sub
  //   mult
  //   div
  //   mflo
  //   mfhi
  //   sll
  //   srl
  //   slt
  //   addi
  //   jr
  //   jalr
  //   lw
  //   sw
  //   j
  //   jal
  //   beq
  //   bne
  //   rs rt (mult div)
  //   rd (mflo mfhi)
  //   rt rd (sll srl)
  //   rs rt rd (add sub slt)
endmodule
