// Logisim project final.circ as structural Verilog: 7 circuits, main circuit Computer
module Computer (
);

  wire clock_1_out, clock_2_out, clock_4_out, cpu_1_buswriteenable, keyboard_1_avail,
       keyboardcontroller_1_keyboardread, keyboardcontroller_1_writetobus,
       memorycontroller_1_writeenabletomem, memorycontroller_1_writetobus, rgb_video_1_p1, rgb_video_1_p2,
       soundcontroller_1_soundwriteenable, terminalcontroller_1_terminalwriteenable;
  wire [6:0] keyboard_1_data, soundcontroller_1_volume, terminalcontroller_1_ascii_out;
  wire [7:0] rgb_video_1_p3, rgb_video_1_p4;
  wire [13:0] soundcontroller_1_soundfrequency;
  wire [15:0] cpu_1_addresstobus, memorycontroller_1_addresstomem;
  wire [23:0] rgb_video_1_p5;
  wire [31:0] controlled_buffer_1_out, cpu_1_datatobus, keyboardcontroller_1_datatobus,
       memorycontroller_1_datatobus, memorycontroller_1_datatomem, ram_1_dout;

  RAM #(.addrWidth(16), .dataWidth(32), .enables("line")) ram_1 (
    .addr(memorycontroller_1_addresstomem), .we(memorycontroller_1_writeenabletomem), .clk(clock_1_out),
    .din(memorycontroller_1_datatomem), .dout(ram_1_dout));
  Clock clock_1 (.out(clock_1_out));
  Clock clock_2 (.out(clock_2_out));
  Keyboard keyboard_1 (
    .clk(clock_2_out), .re(keyboardcontroller_1_keyboardread), .avail(keyboard_1_avail),
    .data(keyboard_1_data));  // open: clr
  MemoryController memorycontroller_1 (
    .WriteEnableFromBus(cpu_1_buswriteenable), .DataFromBus(controlled_buffer_1_out),
    .AddressFromBus(cpu_1_addresstobus), .DataFromMem(ram_1_dout), .DataToMem(memorycontroller_1_datatomem),
    .AddressToMem(memorycontroller_1_addresstomem), .DataToBus(memorycontroller_1_datatobus),
    .WriteEnableToMem(memorycontroller_1_writeenabletomem), .WriteToBus(memorycontroller_1_writetobus));
  CPU cpu_1 (
    .DataFromBus(controlled_buffer_1_out), .AddressToBus(cpu_1_addresstobus), .DataToBus(cpu_1_datatobus),
    .BusWriteEnable(cpu_1_buswriteenable));
  assign controlled_buffer_1_out = memorycontroller_1_writetobus ? memorycontroller_1_datatobus : 32'bz;  // Controlled_Buffer controlled_buffer_1
  assign controlled_buffer_1_out = cpu_1_buswriteenable ? cpu_1_datatobus : 32'bz;  // Controlled_Buffer controlled_buffer_2
  KeyboardController keyboardcontroller_1 (
    .WriteEnableFromBus(cpu_1_buswriteenable), .KeyboardStatus(keyboard_1_avail),
    .KeyboardData(keyboard_1_data), .DataFromBus(controlled_buffer_1_out),
    .AddressFromBus(cpu_1_addresstobus), .KeyboardRead(keyboardcontroller_1_keyboardread),
    .WriteToBus(keyboardcontroller_1_writetobus), .DataToBus(keyboardcontroller_1_datatobus));
  assign controlled_buffer_1_out = keyboardcontroller_1_writetobus ? keyboardcontroller_1_datatobus : 32'bz;  // Controlled_Buffer controlled_buffer_3
  // RGB_Video #(.height(256), .width(256)) rgb_video_1: pin names not known; wires that end beside it: rgb_video_1_p1, rgb_video_1_p2, rgb_video_1_p3, rgb_video_1_p4, rgb_video_1_p5
  Clock clock_3 (.out(rgb_video_1_p1));
  RGBController rgbcontroller_1 (
    .DataBusIn(controlled_buffer_1_out), .WriteEnable(cpu_1_buswriteenable), .AddressIn(cpu_1_addresstobus),
    .RGBX(rgb_video_1_p3), .RGBY(rgb_video_1_p4), .RGBColor(rgb_video_1_p5), .RGBWrite(rgb_video_1_p2));
  SoundController soundcontroller_1 (
    .DataBusIn(controlled_buffer_1_out), .WriteEnable(cpu_1_buswriteenable), .AddressIn(cpu_1_addresstobus),
    .SoundFrequency(soundcontroller_1_soundfrequency), .Volume(soundcontroller_1_volume),
    .SoundWriteEnable(soundcontroller_1_soundwriteenable));
  TerminalController terminalcontroller_1 (
    .DataBusIn(controlled_buffer_1_out), .WriteEnable(cpu_1_buswriteenable), .AddressIn(cpu_1_addresstobus),
    .ASCII_Out(terminalcontroller_1_ascii_out), .TerminalWriteEnable(terminalcontroller_1_terminalwriteenable));
  // Buzzer buzzer_1: pin names not known; wires that end beside it: soundcontroller_1_soundfrequency, soundcontroller_1_soundwriteenable, soundcontroller_1_volume
  Clock clock_4 (.out(clock_4_out));
  TTY tty_1 (
    .data(terminalcontroller_1_ascii_out), .clk(clock_4_out), .clr(terminalcontroller_1_terminalwriteenable));  // open: we

  // Notes on the sheet:
  //   Write_enable
  //   Address
  //   Data
endmodule

module CPU (
  input  [31:0] DataFromBus,
  output [15:0] AddressToBus,
  output [31:0] DataToBus,
  output BusWriteEnable
);

  wire alu_1_equal, and_1_out, and_2_out, clock_1_out, control_1_aluvmemselect, control_1_beq, control_1_bne,
       control_1_imm_sel, control_1_j, control_1_jal, control_1_jalr, control_1_jr, control_1_we_regfile,
       or_1_out, or_2_out, or_3_out, or_4_out;
  wire [3:0] control_1_alu_operation;
  wire [4:0] control_1_rd_select, control_1_rs_select, control_1_rt_select;
  wire [15:0] bit_extender_3_out, control_1_imm, shifter_1_out;
  wire [25:0] bit_extender_4_out, shifter_2_out;
  wire [31:0] adder_1_out, adder_2_out, alu_1_res, bit_extender_1_out, bit_extender_2_out,
       bit_extender_5_out, multiplexer_1_out, multiplexer_2_out, multiplexer_3_out, multiplexer_4_out,
       multiplexer_5_out, multiplexer_6_out, ProgramCounter_q, regfile_1_rs_data, rom_1_data, shifter_3_out;

  Shifter #(.width(16)) shifter_1 (.in(control_1_imm), .\dist (4'b0010), .out(shifter_1_out));
  Adder #(.width(32)) adder_1 (.a(ProgramCounter_q), .b(32'h4), .out(adder_1_out));  // open: cin, cout
  assign bit_extender_1_out = {{16{shifter_1_out[15]}}, shifter_1_out};  // Bit_Extender bit_extender_1
  Adder #(.width(32)) adder_2 (.a(adder_1_out), .b(bit_extender_1_out), .out(adder_2_out));  // open: cin, cout
  Shifter #(.width(26)) shifter_2 (.in(bit_extender_4_out), .\dist (5'b00010), .out(shifter_2_out));
  and and_1 (and_1_out, control_1_bne, ~alu_1_equal);  // AND_Gate
  and and_2 (and_2_out, control_1_beq, alu_1_equal);
  or or_1 (or_1_out, and_1_out, and_2_out);
  Multiplexer #(.width(32)) multiplexer_1 (
    .in0(adder_1_out), .in1(adder_2_out), .out(multiplexer_1_out), .sel(or_1_out));
  assign bit_extender_2_out = {{6{shifter_2_out[25]}}, shifter_2_out};  // Bit_Extender bit_extender_2
  or or_2 (or_2_out, control_1_jalr, control_1_jr);
  or or_3 (or_3_out, control_1_jal, control_1_jalr, control_1_jr, control_1_j);
  Multiplexer #(.width(32)) multiplexer_2 (
    .in0(multiplexer_1_out), .in1(multiplexer_3_out), .out(multiplexer_2_out), .sel(or_3_out));
  Multiplexer #(.width(32)) multiplexer_3 (
    .in0(bit_extender_2_out), .in1(regfile_1_rs_data), .out(multiplexer_3_out), .sel(or_2_out));
  Register #(.width(32)) ProgramCounter (
    .D(multiplexer_2_out), .en(1'b1), .clk(clock_1_out), .Q(ProgramCounter_q));  // open: clr
  Clock clock_1 (.out(clock_1_out));
  Shifter #(.shift("lr"), .width(32)) shifter_3 (.in(ProgramCounter_q), .\dist (5'b00010), .out(shifter_3_out));
  ROM #(.addrWidth(16), .dataWidth(32)) rom_1 (.addr(bit_extender_3_out), .data(rom_1_data));
  Bit_Extender #(.in_width(32)) bit_extender_3 (.in(shifter_3_out), .out(bit_extender_3_out));
  Bit_Extender #(.in_width(32), .out_width(26)) bit_extender_4 (.in(rom_1_data), .out(bit_extender_4_out));
  // Probe on rom_1_data
  Multiplexer #(.width(32)) multiplexer_4 (
    .in0(alu_1_res), .in1(DataFromBus), .out(multiplexer_4_out), .sel(control_1_aluvmemselect));
  or or_4 (or_4_out, control_1_jal, control_1_jalr);
  Multiplexer #(.width(32)) multiplexer_5 (
    .in0(multiplexer_4_out), .in1(adder_1_out), .out(multiplexer_5_out), .sel(or_4_out));
  regfile regfile_1 (
    .write_e(control_1_we_regfile), .rd(control_1_rd_select), .rt(control_1_rt_select),
    .rs(control_1_rs_select), .rd_data(multiplexer_5_out), .rs_data(regfile_1_rs_data), .rt_data(DataToBus));
  Control control_1 (
    .Instruction(rom_1_data), .we_regfile(control_1_we_regfile), .we_mem(BusWriteEnable),
    .imm_sel(control_1_imm_sel), .jr(control_1_jr), .jalr(control_1_jalr),
    .ALUvMEMselect(control_1_aluvmemselect), .j(control_1_j), .jal(control_1_jal), .beq(control_1_beq),
    .bne(control_1_bne), .rd_select(control_1_rd_select), .rt_select(control_1_rt_select),
    .rs_select(control_1_rs_select), .imm(control_1_imm), .ALU_operation(control_1_alu_operation));
  assign bit_extender_5_out = {{16{control_1_imm[15]}}, control_1_imm};  // Bit_Extender bit_extender_5
  Multiplexer #(.width(32)) multiplexer_6 (
    .in0(DataToBus), .in1(bit_extender_5_out), .out(multiplexer_6_out), .sel(control_1_imm_sel));
  ALU alu_1 (
    .Control(control_1_alu_operation), .OP1(regfile_1_rs_data), .OP2(multiplexer_6_out), .temp_OP(DataToBus),
    .equal(alu_1_equal), .Res(alu_1_res));
  Bit_Extender #(.in_width(32)) bit_extender_6 (.in(alu_1_res), .out(AddressToBus));
  RAM #(.addrWidth(16), .dataWidth(32), .enables("line")) ram_1 ();  // open: addr, we, clk, din, dout

  // Notes on the sheet:
  //   offset: (word addressed)
  //   PC + 4
  //   label: for j, jal (word addressed)
  //   if branch is to be taken
  //   PC + 4 + Offset
  //   jr/jalr
  //   register: for jr, jalr (byte addressed)
  //   any j*
  //   1 if two registers are ==
  //   contents of rom_1 (hex, n*v repeats v):
  //   201b0000 105b0018 201b000a 105b0006 201b000c 105b0005 201b0009 105b000e 201b000b 105b0008 800000a
  //   8c1bff80 17600002 20020000 8000011 8c02ff84 ac00ff80 3400008 80d820 ac1bffb0 8c02ffb0 3400008
  //   8c1bff00 3641020 ac02ff00 3400008 23bdff00 201b0000 afbb0004 20100080 2011007e 20120040 2013003f
  //   20140001 20150000 2110018 4012 84080 20020009 d00c 2002000c d00c 20090077 14490003 12600015 20140000
  //   2015ffff 20090061 14490004 12400010 2014ffff 20150000 8000042 20090073 14490005 200a007e 126a0009
  //   20140000 20150001 8000042 20090064 14490004 200a0080 124a0002 20140001 20150000 200a0001 2530018
  //   5812 b5880 ad6a0000 2549020 2759820 20090001 20080000 240402a 11090010 212402a 11090010 260402a
  //   11090010 233402a 11090010 2530018 5812 b5880 8d6a0000 11490005 ac12ff90 ac13ff94 ac08ff98 ac00ff9c
  //   8000028 20040079 2002000b d00c 2004006f 2002000b d00c 20040075 2002000b d00c 20040020 2002000b d00c
  //   2004006c 2002000b d00c 2004006f 2002000b d00c 20040073 2002000b d00c 20040074 2002000b d00c 20040021
  //   2002000b d00c 200c0320 ac0cffa0 200d003c ac0dffa4 ac00ffa8 2002000a d00c
  //   immediate
  //   label to jump to
  //   rs-data
  //   probe to help test the value in a wire
  //   ALU
  //   MEM
  //   PC + 4
  //   jal/jalr
  //   value from memory
  //   value from ALU
endmodule

module MemoryController (
  input  WriteEnableFromBus,
  input  [31:0] DataFromBus,
  input  [15:0] AddressFromBus,
  input  [31:0] DataFromMem,
  output WriteEnableToMem,
  output WriteToBus,
  output [31:0] DataToMem,
  output [15:0] AddressToMem,
  output [31:0] DataToBus
);

  wire comparator_1_gt;

  Comparator #(.mode("unsigned"), .width(16)) comparator_1 (
    .a(16'hff80), .b(AddressFromBus), .gt(comparator_1_gt));  // open: eq, lt
  and and_1 (WriteEnableToMem, comparator_1_gt, WriteEnableFromBus);
  Shifter #(.shift("lr"), .width(16)) shifter_1 (.in(AddressFromBus), .\dist (4'b0010), .out(AddressToMem));
  and and_2 (WriteToBus, ~WriteEnableToMem, comparator_1_gt);  // AND_Gate

  assign DataToBus = DataFromMem;
  assign DataToMem = DataFromBus;
endmodule

module KeyboardController (
  input  WriteEnableFromBus,
  input  [15:0] AddressFromBus,
  input  KeyboardStatus,
  input  [6:0] KeyboardData,
  input  [31:0] DataFromBus,
  output KeyboardRead,
  output WriteToBus,
  output [31:0] DataToBus
);

  wire and_2_out, and_3_out, comparator_1_eq, comparator_2_eq;
  wire [31:0] and_4_out, bit_extender_1_out, bit_extender_2_out, bit_extender_3_out;

  Comparator #(.mode("unsigned"), .width(16)) comparator_1 (
    .a(AddressFromBus), .b(16'hff80), .eq(comparator_1_eq));  // open: gt, lt
  assign bit_extender_1_out = {{31{1'b0}}, KeyboardStatus};  // Bit_Extender bit_extender_1
  Comparator #(.mode("unsigned"), .width(16)) comparator_2 (
    .a(AddressFromBus), .b(16'hff84), .eq(comparator_2_eq));  // open: gt, lt
  and and_1 (KeyboardRead, WriteEnableFromBus, comparator_1_eq);
  and and_2 (and_2_out, ~WriteEnableFromBus, comparator_2_eq);  // AND_Gate
  assign bit_extender_2_out = {{25{1'b0}}, KeyboardData};  // Bit_Extender bit_extender_2
  and and_3 (and_3_out, ~WriteEnableFromBus, comparator_1_eq);  // AND_Gate
  or or_1 (WriteToBus, and_3_out, and_2_out);
  assign bit_extender_3_out = {{31{and_3_out}}, and_3_out};  // Bit_Extender bit_extender_3
  assign and_4_out = bit_extender_3_out & bit_extender_1_out;  // AND_Gate and_4, 32 bits wide
  Multiplexer #(.width(32)) multiplexer_1 (.in0(and_4_out), .in1(bit_extender_2_out), .out(DataToBus), .sel(and_2_out));
endmodule

module RGBController (
  input  [31:0] DataBusIn,
  input  WriteEnable,
  input  [15:0] AddressIn,
  output [7:0] RGBX,
  output [7:0] RGBY,
  output [23:0] RGBColor,
  output RGBWrite
);

  wire and_1_out, and_2_out, and_3_out, clock_1_out, clock_2_out, clock_3_out, clock_4_out, clock_5_out,
       clock_6_out, comparator_1_eq, comparator_2_eq, comparator_3_eq, comparator_4_eq, d_ff_1_q, d_ff_2_q,
       d_ff_3_q, undriven, xor_1_out;
  wire [31:0] and_5_out, and_6_out, and_7_out, bit_extender_1_out, bit_extender_2_out, bit_extender_3_out,
       RGB_q, X_q, Y_q;

  Comparator #(.mode("unsigned"), .width(16)) comparator_1 (
    .a(AddressIn), .b(16'hff90), .eq(comparator_1_eq));  // open: gt, lt
  Comparator #(.mode("unsigned"), .width(16)) comparator_2 (
    .a(AddressIn), .b(16'hff94), .eq(comparator_2_eq));  // open: gt, lt
  Comparator #(.mode("unsigned"), .width(16)) comparator_3 (
    .a(AddressIn), .b(16'hff98), .eq(comparator_3_eq));  // open: gt, lt
  Comparator #(.mode("unsigned"), .width(16)) comparator_4 (
    .a(AddressIn), .b(16'hff9c), .eq(comparator_4_eq));  // open: gt, lt
  and and_1 (and_1_out, WriteEnable, comparator_1_eq);
  and and_2 (and_2_out, WriteEnable, comparator_2_eq);
  and and_3 (and_3_out, WriteEnable, comparator_3_eq);
  and and_4 (RGBWrite, WriteEnable, comparator_4_eq);
  assign bit_extender_1_out = {{31{and_1_out}}, and_1_out};  // Bit_Extender bit_extender_1
  assign bit_extender_2_out = {{31{and_2_out}}, and_2_out};  // Bit_Extender bit_extender_2
  assign bit_extender_3_out = {{31{and_3_out}}, and_3_out};  // Bit_Extender bit_extender_3
  D_Flip_Flop d_ff_1 (.D(undriven), .clk(clock_1_out), .Q(d_ff_1_q));  // open: Qn, preset, reset
  Clock clock_1 (.out(clock_1_out));
  D_Flip_Flop d_ff_2 (.D(undriven), .clk(clock_2_out), .Q(d_ff_2_q));  // open: Qn, preset, reset
  Clock clock_2 (.out(clock_2_out));
  assign and_5_out = DataBusIn & bit_extender_1_out;  // AND_Gate and_5, 32 bits wide
  assign and_6_out = DataBusIn & bit_extender_2_out;  // AND_Gate and_6, 32 bits wide
  assign and_7_out = DataBusIn & bit_extender_3_out;  // AND_Gate and_7, 32 bits wide
  D_Flip_Flop d_ff_3 (.D(d_ff_2_q), .clk(clock_3_out), .Q(d_ff_3_q));  // open: Qn, preset, reset
  Clock clock_3 (.out(clock_3_out));
  Register #(.width(32)) X (.D(and_5_out), .en(and_1_out), .clk(clock_4_out), .Q(X_q));  // open: clr
  Clock clock_4 (.out(clock_4_out));
  Register #(.width(32)) Y (.D(and_6_out), .en(and_2_out), .clk(clock_5_out), .Q(Y_q));  // open: clr
  Clock clock_5 (.out(clock_5_out));
  Register #(.width(32)) RGB (.D(and_7_out), .en(and_3_out), .clk(clock_6_out), .Q(RGB_q));  // open: clr
  Clock clock_6 (.out(clock_6_out));
  xor xor_1 (xor_1_out, d_ff_1_q, d_ff_3_q);
  Bit_Extender #(.in_width(32), .out_width(8)) bit_extender_4 (.in(X_q), .out(RGBX));
  Bit_Extender #(.in_width(32), .out_width(8)) bit_extender_5 (.in(Y_q), .out(RGBY));
  Bit_Extender #(.in_width(32), .out_width(24)) bit_extender_6 (.in(RGB_q), .out(RGBColor));
  // AND_Gate and_8 has open pins: in0=d_ff_1_q, in1=xor_1_out, out=open
endmodule

module SoundController (
  input  [31:0] DataBusIn,
  input  WriteEnable,
  input  [15:0] AddressIn,
  output [13:0] SoundFrequency,
  output [6:0] Volume,
  output SoundWriteEnable
);

  wire and_1_out, and_2_out, and_3_out, clock_1_out, clock_2_out, clock_3_out, comparator_1_eq,
       comparator_2_eq, comparator_3_eq;
  wire [31:0] and_4_out, and_5_out, bit_extender_1_out, bit_extender_2_out, register_1_q, register_2_q;

  Comparator #(.width(16)) comparator_1 (.a(AddressIn), .b(16'hffa0), .eq(comparator_1_eq));  // open: gt, lt
  Comparator #(.width(16)) comparator_2 (.a(AddressIn), .b(16'hffa4), .eq(comparator_2_eq));  // open: gt, lt
  Comparator #(.width(16)) comparator_3 (.a(AddressIn), .b(16'hffa8), .eq(comparator_3_eq));  // open: gt, lt
  and and_1 (and_1_out, WriteEnable, comparator_1_eq);
  and and_2 (and_2_out, WriteEnable, comparator_2_eq);
  and and_3 (and_3_out, WriteEnable, comparator_3_eq);
  assign bit_extender_1_out = {{31{and_1_out}}, and_1_out};  // Bit_Extender bit_extender_1
  assign bit_extender_2_out = {{31{and_2_out}}, and_2_out};  // Bit_Extender bit_extender_2
  assign and_4_out = DataBusIn & bit_extender_1_out;  // AND_Gate and_4, 32 bits wide
  assign and_5_out = DataBusIn & bit_extender_2_out;  // AND_Gate and_5, 32 bits wide
  Register #(.width(32)) register_1 (.D(and_4_out), .en(and_1_out), .clk(clock_1_out), .Q(register_1_q));  // open: clr
  Clock clock_1 (.out(clock_1_out));
  Register #(.width(32)) register_2 (.D(and_5_out), .en(and_2_out), .clk(clock_2_out), .Q(register_2_q));  // open: clr
  Clock clock_2 (.out(clock_2_out));
  Register #(.width(1)) register_3 (
    .D(and_3_out), .en(and_3_out), .clk(clock_3_out), .Q(SoundWriteEnable));  // open: clr
  Clock clock_3 (.out(clock_3_out));
  Bit_Extender #(.in_width(32), .out_width(14)) bit_extender_3 (.in(register_1_q), .out(SoundFrequency));
  Bit_Extender #(.in_width(32), .out_width(7)) bit_extender_4 (.in(register_2_q), .out(Volume));

  // Notes on the sheet:
  //   FFA8: WE
  //   FFA0: Frequency Out
  //   FFA4: Volume Out
endmodule

module TerminalController (
  input  [31:0] DataBusIn,
  input  WriteEnable,
  input  [15:0] AddressIn,
  output [6:0] ASCII_Out,
  output TerminalWriteEnable
);

  wire and_1_out, comparator_1_eq, comparator_2_eq;
  wire [31:0] and_3_out, bit_extender_1_out;

  Comparator #(.width(16)) comparator_1 (.a(AddressIn), .b(16'hffb0), .eq(comparator_1_eq));  // open: gt, lt
  Comparator #(.width(16)) comparator_2 (.a(AddressIn), .b(16'hffb4), .eq(comparator_2_eq));  // open: gt, lt
  and and_1 (and_1_out, WriteEnable, comparator_1_eq);
  and and_2 (TerminalWriteEnable, WriteEnable, comparator_2_eq);
  assign bit_extender_1_out = {{31{and_1_out}}, and_1_out};  // Bit_Extender bit_extender_1
  assign and_3_out = DataBusIn & bit_extender_1_out;  // AND_Gate and_3, 32 bits wide
  Bit_Extender #(.in_width(32), .out_width(7)) bit_extender_2 (.in(and_3_out), .out(ASCII_Out));

  // Notes on the sheet:
  //   FFB4: WE
  //   FFB0: Frequency Out
endmodule
